// Logisim project FinalCircuit.circ as structural Verilog
module ALUForge (
);

  wire [7:0] PC_data_out;

  ROM #(.dataWidth(16)) rom_1 ();  // open: addr, data
  SUM sum_1 ();  // open: A, B, A_sign, B_sign, out_5, S9
  registor PC (.data_out(PC_data_out));  // open: CLOCK, WRITE, Data_in, Sign, Sign_out
  registor A ();  // open: CLOCK, WRITE, Data_in, Sign, data_out, Sign_out
  registor ACC ();  // open: CLOCK, WRITE, Data_in, Sign, data_out, Sign_out
  registor B ();  // open: CLOCK, WRITE, Data_in, Sign, data_out, Sign_out
endmodule

module registor (
  input  CLOCK,
  input  WRITE,
  input  [7:0] Data_in,
  input  Sign,
  output [7:0] data_out,
  output Sign_out
);

  Dflipflop C1 (.CLOCK(CLOCK), .Write(WRITE), .D(Data_in[0]), .val(data_out[0]));
  Dflipflop C2 (.CLOCK(CLOCK), .Write(WRITE), .D(Data_in[1]), .val(data_out[1]));
  Dflipflop C3 (.CLOCK(CLOCK), .Write(WRITE), .D(Data_in[2]), .val(data_out[2]));
  Dflipflop C4 (.CLOCK(CLOCK), .Write(WRITE), .D(Data_in[3]), .val(data_out[3]));
  Dflipflop C5 (.CLOCK(CLOCK), .Write(WRITE), .D(Data_in[4]), .val(data_out[4]));
  Dflipflop C6 (.CLOCK(CLOCK), .Write(WRITE), .D(Data_in[5]), .val(data_out[5]));
  Dflipflop C7 (.CLOCK(CLOCK), .Write(WRITE), .D(Data_in[6]), .val(data_out[6]));
  Dflipflop C8 (.CLOCK(CLOCK), .Write(WRITE), .D(Data_in[7]), .val(data_out[7]));
  Dflipflop dflipflop_1 (.CLOCK(CLOCK), .Write(WRITE), .D(Sign), .val(Sign_out));
endmodule

module Dflipflop (
  input  CLOCK,
  input  Write,
  input  D,
  output val
);

  wire and_1_out, nand_2_out, not_1_out, R_out, S_out;

  and and_1 (and_1_out, CLOCK, Write);
  not not_1 (not_1_out, D);
  nand S (S_out, D, and_1_out);
  nand R (R_out, and_1_out, not_1_out);
  nand nand_1 (val, S_out, nand_2_out);
  nand nand_2 (nand_2_out, val, R_out);
endmodule

module ADD_full (
  input  A,
  input  B,
  input  Cin,
  output Sum,
  output Cout
);

  Multiplexer #(.enable("true"), .select(3)) multiplexer_1 (
    .in0(1'b0), .in1(1'b1), .in2(1'b1), .in3(1'b0), .in4(1'b1), .in5(1'b0), .in6(1'b0), .in7(1'b1),
    .out(Sum), .sel({A, B, Cin}));  // open: en
  Multiplexer #(.enable("true"), .select(3)) multiplexer_2 (
    .in0(1'b0), .in1(1'b0), .in2(1'b0), .in3(1'b1), .in4(1'b0), .in5(1'b1), .in6(1'b1), .in7(1'b1),
    .out(Cout), .sel({A, B, Cin}));  // open: en
endmodule

module ADD (
  input  Cin,
  input  [7:0] A,
  input  [7:0] B,
  output [7:0] Sum,
  output Cout
);

  wire add_full_1_cout, add_full_2_cout, add_full_3_cout, add_full_4_cout, add_full_5_cout, add_full_6_cout,
       add_full_7_cout;

  ADD_full add_full_1 (.A(A[0]), .B(B[0]), .Cin(Cin), .Sum(Sum[0]), .Cout(add_full_1_cout));
  ADD_full add_full_2 (.A(A[1]), .B(B[1]), .Cin(add_full_1_cout), .Sum(Sum[1]), .Cout(add_full_2_cout));
  ADD_full add_full_3 (.A(A[2]), .B(B[2]), .Cin(add_full_2_cout), .Sum(Sum[2]), .Cout(add_full_3_cout));
  ADD_full add_full_4 (.A(A[3]), .B(B[3]), .Cin(add_full_3_cout), .Sum(Sum[3]), .Cout(add_full_4_cout));
  ADD_full add_full_5 (.A(A[4]), .B(B[4]), .Cin(add_full_4_cout), .Sum(Sum[4]), .Cout(add_full_5_cout));
  ADD_full add_full_6 (.A(A[5]), .B(B[5]), .Cin(add_full_5_cout), .Sum(Sum[5]), .Cout(add_full_6_cout));
  ADD_full add_full_7 (.A(A[6]), .B(B[6]), .Cin(add_full_6_cout), .Sum(Sum[6]), .Cout(add_full_7_cout));
  ADD_full add_full_8 (.A(A[7]), .B(B[7]), .Cin(add_full_7_cout), .Sum(Sum[7]), .Cout(Cout));
endmodule

module SUM (
  input  [7:0] A,
  input  [7:0] B,
  input  A_sign,
  input  B_sign,
  output [7:0] out_5,
  output S9
);

  wire AminusB_cout, BminusA_cout, not_3_out, not_4_out;
  wire [7:0] AminusB_sum, APlusB_sum, BminusA_sum, multiplexer_1_out, multiplexer_2_out, not_1_out,
       not_2_out, rcomp_1_comp, rcomp_2_comp;

  assign not_1_out = ~A;  // NOT_Gate not_1, 8 bits wide
  assign not_2_out = ~B;  // NOT_Gate not_2, 8 bits wide
  ADD APlusB (.Cin(1'b0), .A(A), .B(B), .Sum(APlusB_sum));  // open: Cout
  ADD BminusA (.Cin(1'b1), .A(not_1_out), .B(B), .Sum(BminusA_sum), .Cout(BminusA_cout));
  ADD AminusB (.Cin(1'b1), .A(A), .B(not_2_out), .Sum(AminusB_sum), .Cout(AminusB_cout));
  Multiplexer #(.width(8)) multiplexer_1 (
    .in0(rcomp_1_comp), .in1(BminusA_sum), .out(multiplexer_1_out), .sel(BminusA_cout));
  not not_3 (not_3_out, BminusA_cout);
  Multiplexer #(.width(8)) multiplexer_2 (
    .in0(rcomp_2_comp), .in1(AminusB_sum), .out(multiplexer_2_out), .sel(AminusB_cout));
  Rcomp rcomp_1 (.Num(BminusA_sum), .comp(rcomp_1_comp));
  not not_4 (not_4_out, AminusB_cout);
  Multiplexer #(.select(2), .width(8)) multiplexer_3 (
    .in0(APlusB_sum), .in1(multiplexer_2_out), .in2(multiplexer_1_out), .in3(APlusB_sum), .out(out_5),
    .sel({B_sign, A_sign}));
  Multiplexer #(.select(2)) multiplexer_4 (
    .in0(1'b0), .in1(not_4_out), .in2(not_3_out), .in3(1'b1), .out(S9), .sel({B_sign, A_sign}));
  Rcomp rcomp_2 (.Num(AminusB_sum), .comp(rcomp_2_comp));
endmodule

module Rcomp (
  input  [7:0] Num,
  output [7:0] comp
);

  wire [7:0] not_1_out;

  assign not_1_out = ~Num;  // NOT_Gate not_1, 8 bits wide
  ADD add_1 (.Cin(1'b0), .A(8'h1), .B(not_1_out), .Sum(comp));  // open: Cout
endmodule
