// Logisim project MULTIPLIER.circ as structural Verilog
module CELL (
  input  a,
  input  b,
  input  acc,
  input  cin,
  output a_out,
  output cout,
  output s
);

  wire and_1_out, and_2_out, and_3_out, xor_1_out;

  and and_1 (and_1_out, a, b);
  xor xor_1 (xor_1_out, and_1_out, acc);
  and and_2 (and_2_out, and_1_out, acc);
  and and_3 (and_3_out, xor_1_out, cin);
  xor xor_2 (s, xor_1_out, cin);
  or or_1 (cout, and_2_out, and_3_out);

  assign a_out = a;
endmodule

module STEP (
  input  a,
  input  [8:0] ACCin,
  input  [8:0] b,
  output P,
  output [8:0] ACCout
);

  wire cell_1_cout, cell_2_cout, cell_3_cout, cell_4_cout, cell_5_cout, cell_6_cout, cell_7_cout, cell_8_cout;

  CELL cell_1 (.a(a), .b(b[0]), .acc(ACCin[0]), .cin(1'b0), .cout(cell_1_cout), .s(P));  // open: a_out
  CELL cell_2 (.a(a), .b(b[1]), .acc(ACCin[1]), .cin(cell_1_cout), .cout(cell_2_cout), .s(ACCout[0]));  // open: a_out
  CELL cell_3 (.a(a), .b(b[2]), .acc(ACCin[2]), .cin(cell_2_cout), .cout(cell_3_cout), .s(ACCout[1]));  // open: a_out
  CELL cell_4 (.a(a), .b(b[3]), .acc(ACCin[3]), .cin(cell_3_cout), .cout(cell_4_cout), .s(ACCout[2]));  // open: a_out
  CELL cell_5 (.a(a), .b(b[4]), .acc(ACCin[4]), .cin(cell_4_cout), .cout(cell_5_cout), .s(ACCout[3]));  // open: a_out
  CELL cell_6 (.a(a), .b(b[5]), .acc(ACCin[5]), .cin(cell_5_cout), .cout(cell_6_cout), .s(ACCout[4]));  // open: a_out
  CELL cell_7 (.a(a), .b(b[6]), .acc(ACCin[6]), .cin(cell_6_cout), .cout(cell_7_cout), .s(ACCout[5]));  // open: a_out
  CELL cell_8 (.a(a), .b(b[7]), .acc(ACCin[7]), .cin(cell_7_cout), .cout(cell_8_cout), .s(ACCout[6]));  // open: a_out
  CELL cell_9 (.a(a), .b(b[8]), .acc(ACCin[8]), .cin(cell_8_cout), .cout(ACCout[8]), .s(ACCout[7]));  // open: a_out
endmodule
