// Logisim project register.circ as structural Verilog: 2 circuits, main circuit registor
module registor (
);

  D_Flip_Flop #(.trigger("high")) F0 ();  // open: D, clk, Q, Qn, preset, reset
  D_Flip_Flop #(.trigger("high")) d_ff_1 ();  // open: D, clk, Q, Qn, preset, reset
  D_Flip_Flop #(.trigger("high")) d_ff_2 ();  // open: D, clk, Q, Qn, preset, reset
  D_Flip_Flop #(.trigger("high")) d_ff_3 ();  // open: D, clk, Q, Qn, preset, reset
  D_Flip_Flop #(.trigger("high")) d_ff_4 ();  // open: D, clk, Q, Qn, preset, reset
  D_Flip_Flop #(.trigger("high")) d_ff_5 ();  // open: D, clk, Q, Qn, preset, reset
  D_Flip_Flop #(.trigger("high")) d_ff_6 ();  // open: D, clk, Q, Qn, preset, reset
  D_Flip_Flop #(.trigger("high")) d_ff_7 ();  // open: D, clk, Q, Qn, preset, reset
endmodule

module Dflipflop (
  input  CLOCK,
  input  Write,
  input  D,
  output out_4
);

  wire and_1_out, nand_2_out, not_1_out, R_out, S_out;

  and and_1 (and_1_out, CLOCK, Write);
  not not_1 (not_1_out, D);
  nand S (S_out, D, and_1_out);
  nand R (R_out, and_1_out, not_1_out);
  nand nand_1 (out_4, S_out, nand_2_out);
  nand nand_2 (nand_2_out, out_4, R_out);
endmodule
